# Fritzing sketch dram (saved by Fritzing 0.9.2b)
breadboards: 1

parts:
  Part1 = Arduino Uno (Rev3)
  DIMM = female pin header, 30 pins [form="♀ (female)"]

nets:
  N1: Part1.D8, DIMM.pin8
  N2: Part1.D9_PWM, DIMM.pin10
  N3: Part1.D10_PWM/SS, DIMM.pin13
  N4: Part1.D11_PWM/MOSI, DIMM.pin21
  N5: Part1.D12/MISO, DIMM.pin27
  N6: Part1.D2, DIMM.pin2
  N7: Part1.D3_PWM, DIMM.pin3
  N8: Part1.D4, DIMM.pin4
  N9: Part1.D5_PWM, DIMM.pin5
  N10: Part1.D6_PWM, DIMM.pin6
  N11: Part1.D7, DIMM.pin7
  N12: Part1.5V, DIMM.pin1, DIMM.pin28, DIMM.pin30
  N13: Part1.GND, DIMM.pin9, DIMM.pin11, DIMM.pin12, DIMM.pin14, DIMM.pin15, DIMM.pin17, DIMM.pin18, DIMM.pin22

notes:
  1
  30
